// Logisim project BM.circ as structural Verilog: 1 circuit, main circuit main
module main (
  input  BLD,
  input  BM,
  output R1,
  output R2,
  output MV
);

  wire \_1ºciclo_out , and_1_out, and_2_out, and_3_out, and_4_out, D0_q, D0_qn, D1_q, D1_qn, not_1_out,
       not_2_out, or_1_out, or_2_out, or_3_out, or_4_out, xor_1_out;

  xor xor_1 (xor_1_out, D0_q, D1_q);
  or or_1 (or_1_out, D1_qn, D0_q);
  not not_1 (not_1_out, BM);
  or or_2 (or_2_out, D0_qn, D1_q);
  and and_1 (and_1_out, D1_q, not_2_out, BLD);
  not not_2 (not_2_out, BM);
  and and_2 (and_2_out, BM, BLD, xor_1_out);
  Clock \_1ºciclo  (.out(\_1ºciclo_out ));
  and and_3 (and_3_out, or_1_out, not_1_out, BLD);
  and and_4 (and_4_out, BM, BLD, or_2_out);
  or or_3 (or_3_out, and_1_out, and_2_out);
  or or_4 (or_4_out, and_3_out, and_4_out);
  D_Flip_Flop D1 (.clk(\_1ºciclo_out ), .D(or_3_out), .Q(D1_q), .Qn(D1_qn));  // open: preset, en, reset
  D_Flip_Flop D0 (.clk(\_1ºciclo_out ), .D(or_4_out), .Q(D0_q), .Qn(D0_qn));  // open: preset, en, reset
  xor xor_2 (R1, D0_q, D1_q);
  and and_5 (R2, D0_qn, D1_q);
  or or_5 (MV, D0_q, D1_q);
endmodule
