// Logisim project BO.circ as structural Verilog: 1 circuit, main circuit main
module main (
  input  BLD,
  input  BO,
  output SD,
  output SE,
  output MO
);

  wire \_1ºciclo_out , and_1_out, and_2_out, and_3_out, and_4_out, D0_q, D0_qn, D1_q, D1_qn, D2_q, D2_qn,
       or_1_out, xor_1_out;

  Clock \_1ºciclo  (.out(\_1ºciclo_out ));
  and and_1 (and_1_out, D0_q, D1_q, BO, BLD);
  and and_2 (and_2_out, BO, BLD, xor_1_out);
  and and_3 (and_3_out, BO, BLD, D0_qn, or_1_out);
  or or_1 (or_1_out, D2_qn, D1_qn);
  D_Flip_Flop D2 (.clk(\_1ºciclo_out ), .D(and_1_out), .Q(D2_q), .Qn(D2_qn));  // open: preset, en, reset
  xor xor_1 (xor_1_out, D1_q, D0_q);
  D_Flip_Flop D1 (.clk(\_1ºciclo_out ), .D(and_2_out), .Q(D1_q), .Qn(D1_qn));  // open: preset, en, reset
  D_Flip_Flop D0 (.clk(\_1ºciclo_out ), .D(and_3_out), .Q(D0_q), .Qn(D0_qn));  // open: preset, en, reset
  xor xor_2 (SD, D0_q, D1_q);
  and and_4 (and_4_out, D0_q, D1_q);
  or or_2 (MO, D0_q, D1_q, D2_q);
  or or_3 (SE, and_4_out, D2_q);
endmodule
