// Logisim project MAIN.circ as structural Verilog: 1 circuit, main circuit main
module main (
  input  BLD,
  input  BM,
  input  BO,
  output R1,
  output R2,
  output MV,
  output SD,
  output SE,
  output MO
);

  wire \_1ºciclo_out , and_1_out, and_2_out, and_3_out, and_4_out, and_5_out, and_6_out, and_7_out,
       and_9_out, D10_q, D10_qn, D11_q, D11_qn, D20_q, D20_qn, D21_q, D21_qn, D22_q, D22_qn, not_1_out,
       not_2_out, or_1_out, or_2_out, or_3_out, or_4_out, or_5_out, xor_1_out, xor_2_out;

  not not_1 (not_1_out, BM);
  and and_1 (and_1_out, BO, BLD, D20_q, D21_q);
  and and_2 (and_2_out, BO, BLD, xor_1_out);
  or or_1 (or_1_out, D11_qn, D10_q);
  not not_2 (not_2_out, BM);
  or or_2 (or_2_out, D10_qn, D11_q);
  and and_3 (and_3_out, D11_q, not_1_out, BLD);
  and and_4 (and_4_out, BM, BLD, xor_2_out);
  xor xor_1 (xor_1_out, D21_q, D20_q);
  Clock \_1ºciclo  (.out(\_1ºciclo_out ));
  and and_5 (and_5_out, or_1_out, not_2_out, BLD);
  or or_3 (or_3_out, and_5_out, and_6_out);
  and and_6 (and_6_out, BLD, BM, or_2_out);
  or or_4 (or_4_out, and_3_out, and_4_out);
  D_Flip_Flop D11 (.clk(\_1ºciclo_out ), .D(or_4_out), .Q(D11_q), .Qn(D11_qn));  // open: preset, en, reset
  xor xor_2 (xor_2_out, D11_q, D10_q);
  and and_7 (and_7_out, or_5_out, D20_qn, BO, BLD);
  D_Flip_Flop D10 (.clk(\_1ºciclo_out ), .D(or_3_out), .Q(D10_q), .Qn(D10_qn));  // open: preset, en, reset
  D_Flip_Flop D22 (.clk(\_1ºciclo_out ), .D(and_1_out), .Q(D22_q), .Qn(D22_qn));  // open: preset, en, reset
  D_Flip_Flop D21 (.clk(\_1ºciclo_out ), .D(and_2_out), .Q(D21_q), .Qn(D21_qn));  // open: preset, en, reset
  or or_5 (or_5_out, D22_qn, D21_qn);
  D_Flip_Flop D20 (.clk(\_1ºciclo_out ), .D(and_7_out), .Q(D20_q), .Qn(D20_qn));  // open: preset, en, reset
  xor xor_3 (R1, D10_q, D11_q);
  and and_8 (R2, D10_qn, D11_q);
  or or_6 (MV, D10_q, D11_q);
  xor xor_4 (SD, D20_q, D21_q);
  and and_9 (and_9_out, D20_q, D21_q);
  or or_7 (MO, D20_q, D21_q, D22_q);
  or or_8 (SE, and_9_out, D22_q);
endmodule
